# Fritzing sketch Untitled Sketch (saved by Fritzing 0.9.3b)
breadboards: 1

parts:
  U1 = LM124-324 Quad Opamp [package="DIP (Dual Inline)"]
  R1 = Resistor [tolerance=±5% resistance=220 package=THT]
  R2 = Resistor [tolerance=±5% resistance=39k package=THT]
  P1 = S1133 Si Photodiode [package="8mm Ceramic [THT]"]
  LED1 = LED - 5mm [color="Red (633nm)" package="5 mm [THT]"]
  C1 = Tantalum Capacitor [capacitance=1μF package="100 mil [THT, tantalum]"]
  R3 = Resistor [tolerance=±5% resistance=68k package=THT]
  R4 = Resistor [tolerance=±5% resistance=8.2k package=THT]
  C2 = Ceramic Capacitor [capacitance=0.1µF package="100 mil [THT, multilayer]"]
  C3 = Tantalum Capacitor [capacitance=1μF package="100 mil [THT, tantalum]"]
  R5 = Resistor [tolerance=±5% resistance=1.8k package=THT]
  C4 = Ceramic Capacitor [capacitance=0.1µF package="100 mil [THT, multilayer]"]
  R6 = Resistor [tolerance=±5% resistance=470k package=THT]
  R7 = Resistor [tolerance=±5% resistance=68k package=THT]
  Q1 = NPN-Transistor [package="TO92 [THT]"]
  Part1 = Arduino Uno (Rev3)

nets:
  N1: U1.1OUT, C2.1, C3.+
  N2: U1.1IN-, R4.Pin_0, C2.0
  N3: U1.1IN+, C1.-
  N4: U1.VCC+, R2.Pin_0, Q1.C, Part1.5V
  N5: U1.4IN+, C3.-, R7.Pin_0
  N6: U1.4IN-, C4.0, R6.Pin_1
  N7: U1.4OUT, R5.Pin_0, C4.1, R6.Pin_0
  N8: R1.Pin_1, LED1.anode
  N9: R2.Pin_1, P1.cathode, C1.+
  N10: P1.anode, LED1.cathode, R3.Pin_1, R4.Pin_1, R7.Pin_1, Part1.GND
  N11: Q1.E, Part1.A0
